// Logisim project TallerLogica-Combinatorios.circ as structural Verilog: 9 circuits, main circuit sumador_simple
module sumador_simple (
  input  A,
  input  B,
  output S,
  output Cout
);

  xor xor_1 (S, A, B);
  and and_1 (Cout, A, B);
endmodule

module sumador_completo (
  input  Cin,
  input  A,
  input  B,
  output S,
  output Cout
);

  wire suma_simple_2_cout, suma_simple_cout, suma_simple_s;

  sumador_simple suma_simple (.A(A), .B(B), .S(suma_simple_s), .Cout(suma_simple_cout));
  sumador_simple suma_simple_2 (.A(Cin), .B(suma_simple_s), .S(S), .Cout(suma_simple_2_cout));
  or or_1 (Cout, suma_simple_2_cout, suma_simple_cout);
endmodule

module sumador_4 (
  input  Cin,
  input  [3:0] A,
  input  [3:0] B,
  output [3:0] S,
  output Cout
);

  wire sumador_completo_1_cout, sumador_completo_2_cout, sumador_completo_3_cout;

  sumador_completo sumador_completo_1 (.A(A[0]), .B(B[0]), .Cin(Cin), .S(S[0]), .Cout(sumador_completo_1_cout));
  sumador_completo sumador_completo_2 (
    .A(A[1]), .B(B[1]), .Cin(sumador_completo_1_cout), .S(S[1]), .Cout(sumador_completo_2_cout));
  sumador_completo sumador_completo_3 (
    .A(A[2]), .B(B[2]), .Cin(sumador_completo_2_cout), .S(S[2]), .Cout(sumador_completo_3_cout));
  sumador_completo sumador_completo_4 (.A(A[3]), .B(B[3]), .Cin(sumador_completo_3_cout), .S(S[3]), .Cout(Cout));
  Hex_Digit_Display hex_digit_display_1 (.value(S));  // open: dp
endmodule

module comparador_cero (
  input  [3:0] A,
  output Z
);

  nor nor_1 (Z, A[0], A[1], A[2], A[3]);
endmodule

module sumador_flags (
  input  Cin,
  input  [3:0] A,
  input  [3:0] B,
  output [3:0] S,
  output Z,
  output N,
  output C,
  output V
);

  wire sumador_completo_1_cout, sumador_completo_2_cout, sumador_completo_3_cout;

  sumador_completo sumador_completo_1 (.A(A[0]), .B(B[0]), .Cin(Cin), .S(S[0]), .Cout(sumador_completo_1_cout));
  sumador_completo sumador_completo_2 (
    .A(A[1]), .B(B[1]), .Cin(sumador_completo_1_cout), .S(S[1]), .Cout(sumador_completo_2_cout));
  sumador_completo sumador_completo_3 (
    .A(A[2]), .B(B[2]), .Cin(sumador_completo_2_cout), .S(S[2]), .Cout(sumador_completo_3_cout));
  sumador_completo sumador_completo_4 (.A(A[3]), .B(B[3]), .Cin(sumador_completo_3_cout), .S(N), .Cout(C));
  xor xor_1 (V, sumador_completo_3_cout, C);
  Hex_Digit_Display hex_digit_display_1 (.value({N, S[2:0]}));  // open: dp
  comparador_cero comparador_cero_1 (.A({N, S[2:0]}), .Z(Z));

  assign S[3] = N;
endmodule

module incrementador_4 (
  input  [3:0] A,
  output [3:0] S
);

  wire not_1_out, sumador_simple_1_cout, sumador_simple_2_cout, sumador_simple_3_cout, xor_1_out;

  not not_1 (not_1_out, A[0]);
  xor xor_1 (xor_1_out, A[0], not_1_out);
  sumador_simple sumador_simple_1 (.A(xor_1_out), .B(A[0]), .S(S[0]), .Cout(sumador_simple_1_cout));
  sumador_simple sumador_simple_2 (.A(sumador_simple_1_cout), .B(A[1]), .S(S[1]), .Cout(sumador_simple_2_cout));
  sumador_simple sumador_simple_3 (.A(sumador_simple_2_cout), .B(A[2]), .S(S[2]), .Cout(sumador_simple_3_cout));
  sumador_simple sumador_simple_4 (.A(sumador_simple_3_cout), .B(A[3]), .S(S[3]));  // open: Cout
  Hex_Digit_Display hex_digit_display_1 (.value(S));  // open: dp
endmodule

module inversor_4 (
  input  [3:0] A,
  input  INV,
  output [3:0] S
);

  wire sumador_simple_1_cout, sumador_simple_2_cout, sumador_simple_3_cout, xor_1_out, xor_2_out, xor_3_out,
       xor_4_out;

  xor xor_1 (xor_1_out, A[0], INV);
  xor xor_2 (xor_2_out, A[1], INV);
  xor xor_3 (xor_3_out, A[2], INV);
  xor xor_4 (xor_4_out, A[3], INV);
  sumador_simple sumador_simple_1 (.A(INV), .B(xor_1_out), .S(S[0]), .Cout(sumador_simple_1_cout));
  sumador_simple sumador_simple_2 (.A(sumador_simple_1_cout), .B(xor_2_out), .S(S[1]), .Cout(sumador_simple_2_cout));
  sumador_simple sumador_simple_3 (.A(sumador_simple_2_cout), .B(xor_3_out), .S(S[2]), .Cout(sumador_simple_3_cout));
  sumador_simple sumador_simple_4 (.A(sumador_simple_3_cout), .B(xor_4_out), .S(S[3]));  // open: Cout
  Hex_Digit_Display hex_digit_display_1 (.value(S));  // open: dp
endmodule

module ALU (
  input  [3:0] A,
  input  [3:0] B,
  input  [1:0] OP,
  output N,
  output Z,
  output V,
  output C,
  output [3:0] S
);

  Hex_Digit_Display hex_digit_display_1 (.value(S));  // open: dp
endmodule

module verificador (
  output [3:0] out_1,
  output [3:0] out_2,
  output [1:0] out_3,
  output halt,
  output N,
  output Z,
  output V,
  output C,
  output [3:0] res
);

  wire clock_1_out;

  Clock clock_1 (.out(clock_1_out));
  Counter #(.width(10), .max('h3ff)) counter_1 ();  // open: load, D, count, Q, carry, clk, clr
  ALU alu_1 (.A(out_1), .B(out_2), .OP(out_3), .N(N), .Z(Z), .V(V), .C(C), .S(res));
endmodule
